# Fritzing sketch IGVC (saved by Fritzing 0.9.2b)

parts:
  24_V = DC Power [voltage=5]
  S1 = SWITCH-MOMENTARY-2 [package=tactile-switch-1101ne]
  U1 = AD8226 - Rail-to-Rail output Instrumentation Amplifier [part_number=AD8226]

nets:
  N1: 24_V.V+, U1.-VS
  N2: 24_V.V-, S1.1
  GND: S1.2
